# Fritzing sketch FIRSTPROJEDIT (saved by Fritzing 1.0.6)
breadboards: 1

parts:
  Part1 = Arduino Uno (Rev3)
  L298N1 = L298N DC motor driver
  M1 = DC Motor [voltage_(max)=6V voltage_(min)=3V]
  M2 = DC Motor [voltage_(max)=6V voltage_(min)=3V]
  M3 = fc-51 [package=THT]
  M4 = fc-51 [package=THT]
  S1 = Round Pushbutton
  VCC1 = 4 x AAA Battery Mount [internal_resistance=0.1Ω]

nets:
  N1: Part1.D8, L298N1.IN3
  N2: Part1.D12/MISO, L298N1.IN2
  N3: Part1.D13/SCK, L298N1.IN1
  N4: Part1.D2, M3.pin1
  N5: Part1.D4, M4.pin1
  N6: Part1.D5_PWM, L298N1.ENA
  N7: Part1.D6_PWM, L298N1.ENB
  N8: Part1.D7, L298N1.IN4
  5V: Part1.5V, L298N1.5V, M3.pin3, M4.pin3
  GND: Part1.GND, L298N1.GND, M3.pin2, M4.pin2, VCC1.-
  N9: L298N1.OUT1, M1.pin_2
  N10: L298N1.OUT2, M1.pin_1
  N11: L298N1.OUT3, M2.pin_2
  N12: L298N1.OUT4, M2.pin_1
  N13: L298N1.12V, S1.leg1
  N14: S1.leg0, VCC1.+

custom parts:
  L298N DC motor driver: 2x DC motor driver with 78M05 positive voltage regulator (7..35 V) L298N: max 46 V, 2 A Set 5 V Enable jumper to enable 5 V regultor (needed for the L298N) and +5 V output at screw terminal or supply external +5 V at screw terminal Set ENA and/or ENB to +5 V to enable motor permanently or supply ENA and/or ENB with PWM signal IN1 and IN2 set rotation directory for motor A (OUT1/OUT2) IN2 and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

// code stored in the sketch: FIRSTPROJ.ino
int senseF= 2;
int senseL = 4;
int pwmF = 5;
int pwmL = 6;
int mtrTwoF = 8;
int mtrTwoL = 7;
int mtrOneF = 13;
int mtrOneL = 12;
int speed = 200;
char lastTurn = 'S';
void setup(){
	pinMode(senseF, INPUT);
	pinMode(senseL, INPUT);
	pinMode(pwmF, OUTPUT);
	pinMode(pwmL, OUTPUT);
	pinMode(mtrTwoF, OUTPUT);
	pinMode(mtrTwoL, OUTPUT);
	pinMode(mtrOneF, OUTPUT);
	pinMode(mtrOneL, OUTPUT);
}

void goStraight(){
		digitalWrite(mtrOneF, HIGH);
		digitalWrite(mtrTwoF, HIGH);
		digitalWrite(mtrOneL, LOW);
		digitalWrite(mtrTwoL, LOW);
		analogWrite(pwmF, speed);
		analogWrite(pwmL, speed);
}

void turnLeft(){
		digitalWrite(mtrOneF, HIGH);
		digitalWrite(mtrTwoF, LOW);
		digitalWrite(mtrOneL, LOW);
		digitalWrite(mtrTwoL, HIGH);
		analogWrite(pwmF, speed);
		analogWrite(pwmL, speed);
}

void turnRight(){
		digitalWrite(mtrOneF, LOW);
		digitalWrite(mtrTwoF, HIGH);
		digitalWrite(mtrOneL, HIGH);
		digitalWrite(mtrTwoL, LOW);
		analogWrite(pwmF, speed);
		analogWrite(pwmL, speed);
}

void stopMotors(){
		digitalWrite(mtrOneF, LOW);
		digitalWrite(mtrTwoF, LOW);
		digitalWrite(mtrOneL, LOW);
		digitalWrite(mtrTwoL, LOW);
		analogWrite(pwmF, 0);
		analogWrite(pwmL, 0);
}


void loop(){
	int senseFvalue = digitalRead(senseF);
	int senseLvalue = digitalRead(senseL);
	if (senseLvalue == LOW && senseFvalue == LOW){
		goStraight();
		lastTurn = 'S';
	} else if (senseFvalue == HIGH && senseLvalue == LOW){
		turnLeft();
		lastTurn = 'L';
	} else if (senseFvalue == LOW && senseLvalue == HIGH){
		turnRight();
		lastTurn = 'R';
	} else if (senseFvalue == HIGH && senseLvalue == HIGH){
		if(lastTurn == 'L') turnLeft();
		else if(lastTurn == 'R') turnRight();
		else stopMotors();
	}
}
